// Digital circuit 2bitmultiplier.dig as structural Verilog
module _2bitmultiplier (
  input  [1:0] A,
  input  [1:0] B,
  input  [1:0] A_2,
  input  [1:0] B_2,
  input  [1:0] A_3,
  input  [1:0] B_3,
  input  A0,
  input  B0,
  output P2,
  output P3,
  output P0,
  output P1
);

  wire and_1_out, and_2_out, and_3_out, and_4_out, and_6_out, and_8_out, not_1_out, not_2_out, not_3_out,
       not_4_out, not_5_out, not_6_out, or_1_out, or_2_out;

  not not_1 (not_1_out, B_3[1]);
  not not_2 (not_2_out, A_3[1]);
  not not_3 (not_3_out, B_3[0]);
  not not_4 (not_4_out, A_3[0]);
  and and_1 (and_1_out, not_1_out, B_3[0], A_3[1]);
  and and_2 (and_2_out, B_3[1], A_3[0], not_2_out);
  and and_3 (and_3_out, B_3[1], not_3_out, A_3[0]);
  and and_4 (and_4_out, not_4_out, A_3[1], B_3[0]);
  or or_1 (or_1_out, and_1_out, and_4_out);
  or or_2 (or_2_out, and_2_out, and_3_out);
  and and_5 (P0, A0, B0);
  or or_3 (P1, or_1_out, or_2_out);
  not not_5 (not_5_out, B[0]);
  not not_6 (not_6_out, A[0]);
  and and_6 (and_6_out, A[1], B[1], not_5_out);
  and and_7 (P3, A_2[0], A_2[1], B_2[0], B_2[1]);
  and and_8 (and_8_out, A[1], B[1], not_6_out);
  or or_4 (P2, and_6_out, and_8_out);
endmodule
