// Digital circuit 4 bit adder.dig as structural Verilog
module _4_bit_adder (
  input  A,
  input  B,
  input  Cin,
  input  A_2,
  input  B_2,
  input  A_3,
  input  B_3,
  input  A_4,
  input  B_4,
  input  A_5,
  input  B_5,
  input  Cin_2,
  input  C,
  input  D,
  input  E,
  input  F,
  input  G,
  input  H,
  output Sum,
  output Sum_2,
  output Sum_3,
  output Sum_4,
  output Cout,
  output out_22,
  output out_23,
  output out_24,
  output out_25,
  output Cout_2
);

  wire add_1_c_o, add_2_c_o, add_3_c_o, and_1_out, and_2_out, and_3_out, and_4_out, and_5_out, and_6_out,
       and_7_out, and_8_out, or_1_out, or_2_out, or_3_out, xor_1_out, xor_2_out, xor_3_out, xor_4_out;

  Add add_1 (.a(A_5), .b(B_5), .c_i(Cin_2), .s(out_22), .c_o(add_1_c_o));
  Add add_2 (.a(C), .b(D), .c_i(add_1_c_o), .s(out_23), .c_o(add_2_c_o));
  Add add_3 (.a(E), .b(F), .c_i(add_2_c_o), .s(out_24), .c_o(add_3_c_o));
  Add add_4 (.a(G), .b(H), .c_i(add_3_c_o), .s(out_25), .c_o(Cout_2));
  xor xor_1 (xor_1_out, A, B);
  and and_1 (and_1_out, B, A);
  xor xor_2 (xor_2_out, A_2, B_2);
  and and_2 (and_2_out, B_2, A_2);
  and and_3 (and_3_out, B_3, A_3);
  and and_4 (and_4_out, B_4, A_4);
  xor xor_3 (xor_3_out, A_3, B_3);
  xor xor_4 (xor_4_out, A_4, B_4);
  and and_5 (and_5_out, xor_1_out, Cin);
  and and_6 (and_6_out, xor_2_out, or_1_out);
  and and_7 (and_7_out, xor_3_out, or_2_out);
  and and_8 (and_8_out, xor_4_out, or_3_out);
  xor xor_5 (Sum, xor_1_out, Cin);
  xor xor_6 (Sum_2, xor_2_out, or_1_out);
  xor xor_7 (Sum_3, xor_3_out, or_2_out);
  xor xor_8 (Sum_4, xor_4_out, or_3_out);
  or or_1 (or_1_out, and_5_out, and_1_out);
  or or_2 (or_2_out, and_6_out, and_2_out);
  or or_3 (or_3_out, and_7_out, and_3_out);
  or or_4 (Cout, and_8_out, and_4_out);
endmodule
