// Digital circuit 4bitadderBlock.dig as structural Verilog
module _4bitadderBlock (
  input  [3:0] A,
  input  [3:0] B,
  output out_3,
  output out_4,
  output out_5,
  output out_6
);

  wire _1bitadder_1_cout, _1bitadder_2_cout, _1bitadder_3_cout, _1bitadder_4_cout;

  _1bitadder _1bitadder_1 (.A(A[3]), .B(B[3]), .Cin(_1bitadder_2_cout), .Sum(out_3), .Cout(_1bitadder_1_cout));
  _1bitadder _1bitadder_2 (.A(A[2]), .B(B[2]), .Cin(_1bitadder_3_cout), .Sum(out_4), .Cout(_1bitadder_2_cout));
  _1bitadder _1bitadder_3 (.A(A[1]), .B(B[1]), .Cin(_1bitadder_4_cout), .Sum(out_5), .Cout(_1bitadder_3_cout));
  _1bitadder _1bitadder_4 (.A(A[0]), .B(B[0]), .Cin(_1bitadder_1_cout), .Sum(out_6), .Cout(_1bitadder_4_cout));
endmodule
